# Fritzing sketch LED_TEST (saved by Fritzing 1.0.2b)
circuit board: 5.3744cm x 3.63018cm
breadboards: 1

parts:
  R5 = Resistor [tolerance=±5% power=0.25W resistance=100 package=THT]
  J1 = male pin header, 2 pins [form="♂ (male)"]
  R4 = Resistor [tolerance=±5% power=0.25W resistance=100 package=THT]
  LED2 = RGB LED (com. cathode, rbg) [color="Red (633nm)" current=0.030A package="5 mm [THT]"]
  R7 = TRIMPOT [maximum_resistance=5kΩ knob_status=50% power=0.5W package=trim_pot_pth]
  R8 = TRIMPOT [maximum_resistance=5kΩ knob_status=50% power=0.5W package=trim_pot_pth]
  R9 = TRIMPOT [maximum_resistance=5kΩ knob_status=50% power=0.5W package=trim_pot_pth]
  R6 = Resistor [tolerance=±5% power=0.25W resistance=100 package=THT]

nets:
  N1: R5.Pin_0, J1.pin2, R4.Pin_0, R6.Pin_0
  N2: R5.Pin_1, R7.CW
  N3: J1.pin1, LED2.common_cathode
  N4: R4.Pin_1, R9.CW
  N5: LED2.red_anode, R9.WIPER
  N6: LED2.blue_anode, R8.WIPER
  N7: LED2.green_anode, R7.WIPER
  N8: R8.CW, R6.Pin_1
