# Fritzing sketch P_and_P (saved by Fritzing 1.0.2b)
breadboards: 1

parts:
  J1 = shrouded pin header, 40 pins [form="♂ (shrouded male)"]
  J2 = shrouded pin header, 40 pins [form="♂ (shrouded male)"]
  U2 = Sharp PC817 [package=THT]
  U3 = Sharp PC817 [package=THT]
  U4 = Sharp PC817 [package=THT]
  U5 = Sharp PC817 [package=THT]
  R2 = Resistor [tolerance=±5% power=0.25W resistance=220 package=THT]
  R3 = Resistor [tolerance=±5% power=0.25W resistance=220 package=THT]
  R4 = Resistor [tolerance=±5% power=0.25W resistance=220 package=THT]
  R5 = Resistor [tolerance=±5% power=0.25W resistance=220 package=THT]
  R6 = Resistor [tolerance=±5% power=0.25W resistance=220 package=THT]
  U6 = Sharp PC817 [package=THT]
  Q1 = NPN-Transistor [package="TO92 [THT]"]
  Q2 = NPN-Transistor [package="TO92 [THT]"]
  Q3 = NPN-Transistor [package="TO92 [THT]"]
  Q4 = NPN-Transistor [package="TO92 [THT]"]
  Q5 = NPN-Transistor [package="TO92 [THT]"]
  U7 = Sharp PC817 [package=THT]
  U8 = Sharp PC817 [package=THT]
  U9 = Sharp PC817 [package=THT]
  U10 = Sharp PC817 [package=THT]
  R7 = Resistor [tolerance=±5% power=0.25W resistance=10k package=THT]
  R8 = Resistor [tolerance=±5% power=0.25W resistance=10k package=THT]
  R9 = Resistor [tolerance=±5% power=0.25W resistance=10k package=THT]
  R10 = Resistor [tolerance=±5% power=0.25W resistance=10k package=THT]
  R11 = Resistor [tolerance=±5% power=0.25W resistance=3.3k package=THT]
  R12 = Resistor [tolerance=±5% power=0.25W resistance=3.3k package=THT]
  R13 = Resistor [tolerance=±5% power=0.25W resistance=3.3k package=THT]
  R14 = Resistor [tolerance=±5% power=0.25W resistance=3.3k package=THT]
  Power_plug1 = Power plug

nets:
  3.3V: J1.pin1, U7.Pin_4, U8.Pin_4, U9.Pin_4, U10.Pin_4
  %QX0.0: J1.pin8, J2.pin8, U2.Pin_4, R4.Pin_1, Q1.C
  %QX0.1: J1.pin10, J2.pin9, U4.Pin_4, R2.Pin_1, Q4.C
  %IX0.3: J1.pin11, J2.pin1, U7.Pin_3, R7.Pin_0, R11.Pin_0
  %IX0.4: J1.pin13, J2.pin2, U8.Pin_3, R8.Pin_0, R12.Pin_0
  %IX0.5/GND: J1.pin15, J1.pin39, J2.pin3, U2.Pin_2, U3.Pin_2, U4.Pin_2, U5.Pin_2, U6.Pin_2, R7.Pin_1, R8.Pin_1, R9.Pin_1, R10.Pin_1, R13.Pin_0
  %QX0.2: J1.pin16, J2.pin10, U3.Pin_4, R3.Pin_1, Q2.C
  %QX0.3: J1.pin18, J2.pin11, U5.Pin_4, R5.Pin_1, Q3.C
  %IX0.6: J1.pin19, J2.pin4, U10.Pin_3, R10.Pin_0, R14.Pin_0
  %QX0.4: J1.pin22, J2.pin12, R6.Pin_1, U6.Pin_4, Q5.C
  N1: U2.Pin_1, R4.Pin_0
  N2: U2.Pin_3, Q1.B
  N3: U3.Pin_1, R3.Pin_0
  N4: U3.Pin_3, Q2.B
  N5: U4.Pin_1, R2.Pin_0
  N6: U4.Pin_3, Q4.B
  N7: U5.Pin_1, R5.Pin_0
  N8: U5.Pin_3, Q3.B
  N9: R6.Pin_0, U6.Pin_1
  N10: U6.Pin_3, Q5.B
  N11: Q1.E, Q2.E, Q3.E, Q4.E, Q5.E, Power_plug1.GND
  N12: U7.Pin_1, U8.Pin_1, U9.Pin_1, U10.Pin_1, Power_plug1.VCC
  N13: U7.Pin_2, R11.Pin_1
  N14: U8.Pin_2, R12.Pin_1
  N15: U9.Pin_2, R13.Pin_1
  N16: U9.Pin_3, R9.Pin_0
  N17: U10.Pin_2, R14.Pin_1

notes:
  P&P 40pin
  実際のピン配置に合わせる
  電源24V出力(+/-)も（必要なら）用意する
  Raspberry Pi 40pin
  24V 電源 (AC アダプタ)
