# Fritzing sketch PandP (saved by Fritzing 1.0.2b)
circuit board: 9.5cm x 9.5cm
breadboards: 1

parts:
  U7 = Sharp PC817 [package=THT]
  U8 = Sharp PC817 [package=THT]
  U6 = Sharp PC817 [package=THT]
  U5 = Sharp PC817 [package=THT]
  R6 = Resistor [tolerance=±5% power=0.25W resistance=220 package=THT]
  R7 = Resistor [tolerance=±5% power=0.25W resistance=220 package=THT]
  R9 = Resistor [tolerance=±5% power=0.25W resistance=220 package=THT]
  Q3 = NPN-Transistor [package="TO92 [THT]"]
  Q4 = NPN-Transistor [package="TO92 [THT]"]
  Q1 = NPN-Transistor [package="TO92 [THT]"]
  Q2 = NPN-Transistor [package="TO92 [THT]"]
  Q5 = NPN-Transistor [package="TO92 [THT]"]
  U1 = Sharp PC817 [package=THT]
  U2 = Sharp PC817 [package=THT]
  U4 = Sharp PC817 [package=THT]
  R10 = Resistor [tolerance=±5% power=0.25W resistance=10k package=THT]
  R11 = Resistor [tolerance=±5% power=0.25W resistance=10k package=THT]
  R12 = Resistor [tolerance=±5% power=0.25W resistance=10k package=THT]
  R13 = Resistor [tolerance=±5% power=0.25W resistance=10k package=THT]
  R1 = Resistor [tolerance=±5% power=0.25W resistance=3.3k package=THT]
  R2 = Resistor [tolerance=±5% power=0.25W resistance=3.3k package=THT]
  R3 = Resistor [tolerance=±5% power=0.25W resistance=3.3k package=THT]
  R4 = Resistor [tolerance=±5% power=0.25W resistance=3.3k package=THT]
  Power_plug1 = Power plug
  U9 = Sharp PC817 [package=THT]
  R5 = Resistor [tolerance=±5% power=0.25W resistance=220 package=THT]
  U3 = Sharp PC817 [package=THT]
  R8 = Resistor [tolerance=±5% power=0.25W resistance=220 package=THT]
  J1 = shrouded pin header, 40 pins [form="♂ (shrouded male)"]
  J2 = shrouded pin header, 34 pins [form="♂ (shrouded male)"]

nets:
  N1: U7.Pin_1, R7.Pin_0
  N2: U7.Pin_2, U8.Pin_2, U6.Pin_2, U5.Pin_2, U9.Pin_2, J1.pin20
  Y15: U7.Pin_4, Q3.C, J2.pin24
  N3: U7.Pin_3, Q3.B
  N4: U8.Pin_1, R8.Pin_0
  Y13: U8.Pin_4, Q4.C, J2.pin25
  N5: U8.Pin_3, Q4.B
  N6: U6.Pin_1, R6.Pin_0
  Y14: U6.Pin_4, Q2.C, J2.pin5, J2.pin11, J2.pin30
  N7: U6.Pin_3, Q2.B
  N8: U5.Pin_1, R5.Pin_0
  Y12: U5.Pin_4, Q1.C, J2.pin8, J2.pin10, J2.pin27
  N9: U5.Pin_3, Q1.B
  %QX0.3: R6.Pin_1, J1.pin15, J1.pin26, J1.pin32
  %QX0.4: R7.Pin_1, J1.pin11, J1.pin30
  N10: R9.Pin_0, U9.Pin_1
  %QX0.0: R9.Pin_1, J1.pin22, J1.pin37
  GND(24V-): Q3.E, Q4.E, Q1.E, Q2.E, Q5.E, Power_plug1.GND, J2.pin18
  N11: Q5.B, U9.Pin_3
  Y11: Q5.C, U9.Pin_4, J2.pin26
  24V+: U1.Pin_1, U2.Pin_1, U4.Pin_1, Power_plug1.VCC, U3.Pin_1, J2.pin17
  N12: U1.Pin_2, R1.Pin_1
  3.3V: U1.Pin_4, U2.Pin_4, U4.Pin_4, U3.Pin_4, J1.pin1
  %IX0.3: U1.Pin_3, R10.Pin_0, J1.pin6
  N13: U2.Pin_2, R2.Pin_1
  %IX0.4: U2.Pin_3, R11.Pin_0, J1.pin7
  N14: U4.Pin_2, R4.Pin_1
  %IX0.6: U4.Pin_3, R13.Pin_0, J1.pin10
  GND: R10.Pin_1, R11.Pin_1, R12.Pin_1, R13.Pin_1, J1.pin5
  %IX0.5: R12.Pin_0, U3.Pin_3, J1.pin8
  X1: R1.Pin_0, J2.pin34
  X2: R2.Pin_0, J2.pin2
  X3: R3.Pin_0, J2.pin33
  N15: R3.Pin_1, U3.Pin_2
  X4: R4.Pin_0, J2.pin3, J2.pin32
  %QX0.1: R5.Pin_1, J1.pin18, J1.pin23, J1.pin36
  %QX0.2: R8.Pin_1, J1.pin16, J1.pin25, J1.pin33

notes:
  P&P 40pin
  実際のピン配置に合わせる
  電源24V出力(+/-)も（必要なら）用意する
  Raspberry Pi 40pin
  24V 電源 (AC アダプタ)
