# Fritzing sketch SampleCircuit (saved by Fritzing 1.0.1rc)
circuit board: 5cm x 3cm
breadboards: 1

parts:
  R2 = Resistor [tolerance=±5% power=0.25W resistance=100 package=THT]
  R3 = Resistor [tolerance=±5% power=0.25W resistance=100 package=THT]
  R4 = Resistor [tolerance=±5% power=0.25W resistance=100 package=THT]
  LED1 = RGB LED (com. cathode, rgb) [color="Red (633nm)" current=0.030A package="5 mm [THT]"]
  R5 = TRIMPOT [package=trim_pot_pth]
  R6 = TRIMPOT [package=trim_pot_pth]
  R7 = TRIMPOT [package=trim_pot_pth]
  J1 = male pin header, 2 pins [form="♂ (male)"]

nets:
  N1: R2.Pin_0, R7.CW
  N2: R2.Pin_1, R3.Pin_1, R4.Pin_1, J1.pin2
  N3: R3.Pin_0, R6.CW
  N4: R4.Pin_0, R5.CW
  N5: LED1.red_anode, R7.WIPER
  N6: LED1.common_cathode, J1.pin1
  N7: LED1.green_anode, R6.WIPER
  N8: LED1.blue_anode, R5.WIPER

custom parts:
  TRIMPOT: Various small potentiometers for set-and-forget applications
